# Fritzing sketch SmartDumpster (saved by Fritzing 0.9.3b)
breadboards: 1

parts:
  U1 = ESP8266 NodeMCU LoLin module
  Part1 = Arduino Uno (Rev3)
  Part2 = Bluetooth HC-05 Macho
  LED1 = smd LED [color="Red (633nm)" package="0805 [SMD]"]
  LED2 = smd LED [color="Green (570nm)" package="0805 [SMD]"]
  R1 = Rotary Potentiometer (Small) [maximum_resistance=100kΩ package=THT]
  R2 = Resistor [tolerance=±5% resistance=1k package="2512 [SMD]"]
  R3 = Resistor [tolerance=±5% resistance=1k package="2512 [SMD]"]
  R4 = Resistor [tolerance=±5% resistance=220 package="2512 [SMD]"]
  R5 = Resistor [tolerance=±5% resistance=220 package="2512 [SMD]"]
  R6 = Resistor [tolerance=±5% resistance=220 package="2512 [SMD]"]

nets:
  N1: U1.D1, Part1.D5_PWM
  N2: U1.D2, Part1.D6_PWM
  GND: U1.GND, Part1.GND, Part2.GND, LED1.cathode, LED2.cathode, R1.leg1, R6.Pin_0
  3V3: U1.3V3, Part1.3V3
  N3: Part1.A0, R1.wiper
  N4: Part1.D9_PWM, R2.Pin_1
  N5: Part1.D13/SCK, R3.Pin_1
  N6: Part1.D2, R4.Pin_1
  N7: Part1.D3_PWM, Part2.TXD
  5V: Part1.5V, Part2.VCC, R1.leg2
  N8: Part2.RXD, R4.Pin_0, R5.Pin_1
  N9: LED1.anode, R3.Pin_0
  N10: LED2.anode, R2.Pin_0
  N11: R5.Pin_0, R6.Pin_1

custom parts:
  ESP8266 NodeMCU LoLin module: ESP8266 based NodeMCU
